# Fritzing sketch fritzing_diagram (saved by Fritzing 0.9.6b)
breadboards: 1

parts:
  Part1 = Arduino Uno (Rev3)
  U1 = ESP8266 ESP-01 Upgraded WiFi Module [part_number=ESP8266]
  HC-SR04_Sensor_1 = HC-SR04 Ultrasonic Distance Sensor
  SG1 = Buzzer 12mm [package=buzzer-12mm-ns]

nets:
  N1: Part1.D8, SG1.1
  N2: Part1.D0/RX, U1.RXD
  N3: Part1.D1/TX, U1.TXD
  N4: Part1.D2, HC-SR04_Sensor_1.ECHO
  N5: Part1.D4, HC-SR04_Sensor_1.TRIG
  3V3: Part1.3V3, U1.VCC, U1.CH_PD
  5V: Part1.5V, HC-SR04_Sensor_1.VCC
  GND: Part1.GND, U1.GND, SG1.2

custom parts:
  ESP8266 ESP-01 Upgraded WiFi Module: Upgraded Version ESP-01,all Flash are upgraded to 1M byte.Also support Cloud service remote transmission.
