# Fritzing sketch fritzing_diagram_esp8266_programming_mode (saved by Fritzing 0.9.6b)
breadboards: 1

parts:
  Part2 = Arduino Uno (Rev3)
  U2 = ESP8266 ESP-01 Upgraded WiFi Module [part_number=ESP8266]
  S1 = Pushbutton [package="[THT]"]
  R1 = Resistor [tolerance=±1% resistance=10000 package="2010 [SMD]"]
  LED1 = LED - 5mm [color="Green (560nm)" current=0.030 package="5 mm [THT]"]

nets:
  GND: Part2.GND, Part2.RESET, U2.GPIO_0, U2.GND, S1.Pin_3, S1.Pin_4, LED1.anode
  N1: Part2.D0/RX, U2.RXD
  N2: Part2.D1/TX, U2.TXD
  3V3: Part2.3V3, U2.VCC, U2.CH_PD
  N3: U2.RST/GPIO_16, S1.Pin_1, S1.Pin_2
  N4: U2.GPIO_2, R1.Pin_1
  N5: R1.Pin_0, LED1.cathode

custom parts:
  ESP8266 ESP-01 Upgraded WiFi Module: Upgraded Version ESP-01,all Flash are upgraded to 1M byte.Also support Cloud service remote transmission.
